# Fritzing sketch Schematic (saved by Fritzing 0.9.3b)

parts:
  Part1 = Arduino Mega ADK (Rev3)
  S1 = Momentary Switch [package=ksa_sealed_tac_switch]
  LED1 = LED - 5mm [color="Red (633nm)" package="5 mm [THT]"]
  R1 = Resistor [tolerance=±5% resistance=220 package="2010 [SMD]"]
  R3 = Resistor [tolerance=±5% resistance=220 package="2010 [SMD]"]
  R4 = Resistor [tolerance=±5% resistance=220 package="2010 [SMD]"]
  R5 = Resistor [tolerance=±5% resistance=220 package="2010 [SMD]"]
  R6 = Resistor [tolerance=±5% resistance=220 package="2010 [SMD]"]
  R7 = Resistor [tolerance=±5% resistance=220 package="2010 [SMD]"]
  R8 = Resistor [tolerance=±5% resistance=220 package="2010 [SMD]"]
  R9 = Resistor [tolerance=±5% resistance=220 package="2010 [SMD]"]
  R10 = Resistor [tolerance=±5% resistance=220 package="2010 [SMD]"]
  R11 = Resistor [tolerance=±5% resistance=220 package="2010 [SMD]"]
  LED2 = LED - 5mm [color="Red (633nm)" package="5 mm [THT]"]
  LED3 = LED - 5mm [color="Red (633nm)" package="5 mm [THT]"]
  S2 = Momentary Switch [package=ksa_sealed_tac_switch]
  S3 = Momentary Switch [package=ksa_sealed_tac_switch]

nets:
  N1: Part1.A0, R6.Pin_1
  N2: Part1.A1, R7.Pin_1
  N3: Part1.A2, R8.Pin_1
  N4: Part1.A3, S2.3
  N5: Part1.A4, S1.3
  N6: Part1.A5, S3.3
  N7: Part1.D21/SCL, R9.Pin_0
  N8: Part1.D20/SDA, R1.Pin_0
  N9: Part1.5V, S1.2, R10.Pin_0, S2.2, S3.2
  N10: Part1.GND, LED1.cathode, R3.Pin_0, R4.Pin_0, R5.Pin_0, R11.Pin_0, LED2.anode, LED3.cathode
  N11: S1.4, R4.Pin_1
  N12: LED1.anode, R6.Pin_0
  N13: R3.Pin_1, S2.4
  N14: R5.Pin_1, S3.4
  N15: R7.Pin_0, LED3.anode
  N16: R8.Pin_0, LED2.cathode

notes:
  20x4 LCD
  SDA
  SCL
  VCC
  GND
  RED
  GREEN
  AMBER
  Up Down Test
  Input Pins
  13, 12, 11, 10, 9, 8, 7, 6, 5, 4, 3, 2, 14, 15,
  16, 17, 18, 19, 22, 23, 24, 25, 26, 27, 28, 29
  Output Pins
  30, 31, 32, 33, 34, 35, 36, 37, 38, 39, 40, 41, 42, 43,
  44,45, 46, 47, 48, 49, 50, 51, 52, 53, A15, A14
  All Input pins should be pulled down else they will return garbage state
  All resistors are 1K ohm
